# Fritzing sketch GSM-Alarmanlage (saved by Fritzing 0.9.4)

parts:
  Bauteil1 = Arduino Nano (Rev3.0) (ICSP)
  GSM_SIM_GPSR_SMS_SIM900_SIM1 = SIM800L [package=THT]
  S1 = Taiway 100-SP-X-T1 SPDT Miniature Toggle Switch [part_number=100-SP-X-T1-0-0-B1-M1 package=THT]
  PIR1 = PIR sensor
  U1 = RELAY [package=relay-jzc]
  U2 = LM2596-Step-Down-Converter [package=THT]
  J2 = Screw terminal - 2 pins [package=THT]
  R1 = Resistor [tolerance=±5% resistance=330 package=THT]
  LED1 = LED - 5mm [color="Red (633nm)" package="5 mm [THT]"]
  LED2 = LED - 5mm [color="Yellow (592nm)" package="5 mm [THT]"]
  R2 = Resistor [tolerance=±5% resistance=330 package=THT]
  R3 = Resistor [tolerance=±5% resistance=10k package=THT]
  S2 = SWITCH-MOMENTARY-2 [package=reed_switch_plastic]
  J1 = screw terminal, 2 pins

nets:
  GND: Bauteil1.GND, GSM_SIM_GPSR_SMS_SIM900_SIM1.GND, PIR1.GND, U1.NC, U2.pin4, R3.Pin_1, S2.1
  N1: Bauteil1.D2, S2.2
  N2: Bauteil1.D3, U1.MAIN
  N3: Bauteil1.D4, GSM_SIM_GPSR_SMS_SIM900_SIM1.SIM_TXD
  N4: Bauteil1.D5, GSM_SIM_GPSR_SMS_SIM900_SIM1.SIM_RXD
  N5: Bauteil1.D7, S1.L1, R3.Pin_0
  N6: Bauteil1.D8, PIR1.SIG
  N7: Bauteil1.D11/MOSI, R1.Pin_0
  N8: Bauteil1.D12/MISO, R2.Pin_0
  VIN: Bauteil1.VIN, GSM_SIM_GPSR_SMS_SIM900_SIM1.5V, S1.COM, PIR1.VDD, U2.pin3, LED1.anode, LED2.anode
  N9: U1.COIL2, J2.pin1
  N10: U1.COIL1, J2.pin2
  N11: U2.pin1, J1.pin2
  N12: U2.pin2, J1.pin1
  N13: R1.Pin_1, LED1.cathode
  N14: LED2.cathode, R2.Pin_1

notes:
  armed
  Engine Room
  12V Bilge Relays
  Bilge Switch
  + 12Vdc
  GND
  +5Vdc
  arm / disarm
  PIR
  GSM SIM800
  2 x 330
  LM2596
  motion
  detected
  10k
  Reed contact normally open
  If door is OK the contact is closed
  Bilge relays normally closed
  If bilge is OK the contact is closed

custom parts:
  LM2596-Step-Down-Converter: A dummy, proxy, ersatz, stand-in part for whatever you want. With 4 pins on a 100 mil inline pin header footprint.
